// Digital circuit bit_shifter.dig as structural Verilog
module bit_shifter (
  input  [2:0] SFT,
  input  M,
  input  [15:0] IN,
  input  DIR,
  output [15:0] OUT
);

  wire [0:0] and_6_out, and_8_out, and_10_out, and_12_out, and_14_out;
  wire [1:0] and_2_out;
  wire [2:0] not_1_out;
  wire [15:0] multiplexer_1_out, multiplexer_2_out;
  wire [15:15] and_1_out, and_3_out, and_5_out, and_7_out, and_9_out, and_11_out, and_13_out;

  and and_1 (and_1_out[15], IN[0], M);
  and and_2 (and_2_out[1], M, IN[15]);
  and and_3 (and_3_out[15], IN[1], M);
  and and_4 (and_2_out[0], M, IN[14]);
  and and_5 (and_5_out[15], IN[2], M);
  and and_6 (and_6_out[0], M, IN[13]);
  and and_7 (and_7_out[15], IN[3], M);
  and and_8 (and_8_out[0], M, IN[12]);
  assign not_1_out = ~SFT;  // Not not_1, 3 bits wide
  Multiplexer #(.Selector_Bits(3), .Bits(16)) multiplexer_1 (
    .sel(SFT), .in_0(IN), .in_1({and_1_out[15], IN[15:1]}), .in_2({and_3_out[15], and_1_out[15], IN[15:2]}),
    .in_3({and_5_out[15], and_3_out[15], and_1_out[15], IN[15:3]}),
    .in_4({and_7_out[15], and_5_out[15], and_3_out[15], and_1_out[15], IN[15:4]}),
    .in_5({and_9_out[15], and_7_out[15], and_5_out[15], and_3_out[15], and_1_out[15], IN[15:5]}),
    .in_6({and_11_out[15], and_9_out[15], and_7_out[15], and_5_out[15], and_3_out[15], and_1_out[15], IN[15:6]}),
    .in_7({and_13_out[15], and_11_out[15], and_9_out[15], and_7_out[15], and_5_out[15], and_3_out[15], and_1_out[15], IN[15:7]}),
    .out(multiplexer_1_out));
  Multiplexer #(.Selector_Bits(3), .Bits(16)) multiplexer_2 (
    .sel(not_1_out),
    .in_0({IN[8:0], and_2_out, and_6_out[0], and_8_out[0], and_10_out[0], and_12_out[0], and_14_out[0]}),
    .in_1({IN[9:0], and_2_out, and_6_out[0], and_8_out[0], and_10_out[0], and_12_out[0]}),
    .in_2({IN[10:0], and_2_out, and_6_out[0], and_8_out[0], and_10_out[0]}),
    .in_3({IN[11:0], and_2_out, and_6_out[0], and_8_out[0]}), .in_4({IN[12:0], and_2_out, and_6_out[0]}),
    .in_5({IN[13:0], and_2_out}), .in_6({IN[14:0], and_2_out[1]}), .in_7(IN), .out(multiplexer_2_out));
  and and_9 (and_9_out[15], IN[4], M);
  and and_10 (and_10_out[0], M, IN[11]);
  and and_11 (and_11_out[15], IN[5], M);
  and and_12 (and_12_out[0], M, IN[10]);
  and and_13 (and_13_out[15], IN[6], M);
  and and_14 (and_14_out[0], M, IN[9]);
  Multiplexer #(.Bits(16)) multiplexer_3 (.sel(DIR), .in_0(multiplexer_1_out), .in_1(multiplexer_2_out), .out(OUT));
  // NotConnected on nothing

  // Notes on the sheet:
  //   SFT: How many bits to shift.
  //   M: Set to 1 for rotate mode, 0 for logical mode
  //   IN: Input data.
  //   DIR: Direction, 0 for right and 1 for left.
endmodule

/* Test case Bit Shift:
 	IN SFT M DIR OUT
loop (i, 0xFFFF)
loop (s, 8)

(i) (s) 0 0 (i>>s)
(i) (s) 0 1 (i<<s)
(i) (s) 1 0 ((i<<(16-s))|(i>>s))
(i) (s) 1 1 ((i<<s)|(i>>(16-s)))

end loop
end loop
*/
