// Digital circuit control_unit.dig as structural Verilog
module control_unit (
  input  [15:0] INST,
  input  [1:0] EXEC,
  output [3:0] ALUOP,
  output [2:0] RS1,
  output [2:0] RS2,
  output [2:0] WS,
  output STR,
  output WE,
  output [1:0] DMUX,
  output LDR,
  output FLEN,
  output Ra_control,
  output Rb_control,
  output [15:0] IMM8,
  output [2:0] SFT,
  output SFTM
);

  wire and_1_out, and_3_out, MAX_instruction_comparator_eq, or_1_out, or_2_out, xor_1_out;
  wire [0:0] multiplexer_1_out;
  wire [1:0] nor_2_out;
  wire [3:0] or_3_out;

  and and_1 (and_1_out, EXEC[0], INST[11]);
  nor nor_1 (nor_2_out[1], INST[12], INST[13], INST[14], INST[15]);
  and and_2 (or_3_out[3], INST[12], INST[13], INST[1], INST[14], INST[15]);
  Comparator #(.Bits(4)) MAX_instruction_comparator (
    .a(INST[15:12]), .b(4'b0111), .eq(MAX_instruction_comparator_eq));  // open: gt, lt
  Multiplexer #(.Bits(3)) multiplexer_1 (
    .sel(or_3_out[3]), .in_0(INST[14:12]), .in_1(3'b000), .out({or_3_out[2:1], multiplexer_1_out[0]}));
  or or_1 (or_1_out, and_1_out, ~INST[11]);  // Or
  nor nor_2 (nor_2_out[0], INST[15], nor_2_out[1]);
  and and_3 (and_3_out, INST[0], or_3_out[3]);
  and and_4 (Ra_control, MAX_instruction_comparator_eq, ~EXEC[0], ~EXEC[1]);  // And
  or or_2 (or_2_out, EXEC[0], EXEC[1]);
  and and_5 (STR, ~INST[12], ~INST[13], INST[14], ~INST[15]);  // And
  xor xor_1 (xor_1_out, INST[13], INST[14]);
  and and_6 (Rb_control, MAX_instruction_comparator_eq, or_2_out);
  or or_3 (or_3_out[0], and_3_out, multiplexer_1_out[0]);
  and and_7 (WE, or_1_out, ~STR);  // And
  Multiplexer #(.Bits(3)) multiplexer_2 (.sel(STR), .in_0(INST[2:0]), .in_1(INST[10:8]), .out(RS2));
  and and_8 (LDR, INST[12], ~INST[15], xor_1_out);  // And
  or or_4 (FLEN, INST[15], MAX_instruction_comparator_eq);
  Multiplexer #(.Bits(4)) multiplexer_3 (
    .sel(MAX_instruction_comparator_eq), .in_0(or_3_out), .in_1(4'b0001), .out(ALUOP));
  Multiplexer #(.Bits(2)) multiplexer_4 (
    .sel(MAX_instruction_comparator_eq), .in_0(nor_2_out), .in_1(2'b00), .out(DMUX));
  // NotConnected on nothing
  // NotConnected on nothing
  // NotConnected on nothing
  // NotConnected on nothing
  // NotConnected on nothing
  // NotConnected on nothing
  // NotConnected on nothing
  // NotConnected on nothing
  // NotConnected on nothing
  // NotConnected on nothing
  // NotConnected on nothing
  // NotConnected on nothing

  assign IMM8 = {{8{1'b0}}, INST[7:0]};
  assign RS1 = INST[6:4];
  assign SFT = INST[2:0];
  assign SFTM = INST[3];
  assign WS = INST[10:8];

  // Notes on the sheet:
  //   SFT: The bit to shift for the ALU
  //   SFTM: Shift mode, set 0 for rotate mode, 1 for logical mode.
  //   Negative_sig
  //   Zero_sig
  //   Max_sig
  //   Rd
  //   Ra
  //   Rb
  //   opcode
  //   output ra
  //   output rb
endmodule

/* Test case All Tests:
	INST	EXEC                                    WE  ALUOP  RS1   RS2  WS  STR  LDR DMUX FLEN

let aluop  = 0b1000;
let ldrop  = 0b0101;
let strop  = 0b0100;
let movlop = 0b0000;
let ildrop = 0b0011;

loop(rd, 1<<3)
loop(ra, 1<<3)
loop(rb, 1<<3)

loop(i, 4)
	let inst = ((aluop+i)<<12 | rd<<8 | ra<<4 | rb<<0) >> 15;
	((aluop+i)<<12 | rd<<8 | ra<<4 | rb<<0) (inst & 1)	1  (i)     (ra)  (rb) (rd)  0   X    0  1	#test add/sub/and/orr
end loop
	let inst = (ldrop    <<12 | rd<<8 | ra<<4 ) >> 15;
	let inst = (strop    <<12 | rd<<8 | ra<<4 ) >> 15;
	(ldrop    <<12 | rd<<8 | ra<<4 )        (inst & 1)	1  X       (ra)  x    (rd)  0   1    1  0	#test ldr
	(ildrop   <<12 | rd<<8 | ra<<4 )        (inst & 1)	1  X       (ra)  x    (rd)  0   1    1  0	#test ldr
	(strop    <<12 | rd<<8 | ra<<4 )        (inst & 1)	0  X       (ra)  (rd)  X    1   X    X  0	#test str
	
	let imm = random(256);
	let inst = (movlop   <<12 | rd<<8 | imm ) >> 15;
	(movlop   <<12 | rd<<8 | imm )          (inst & 1)	1  X       X      X   (rd)  0   X    2  0	#test movl

end loop
end loop
end loop
*/

/* Test case WS:
	INST                                    WS 

let aluop  = 0b1000;
let ldrop  = 0b0101;
let strop  = 0b0100;
let movlop = 0b0000;

loop(rd, 1<<3)
loop(ra, 1<<3)
loop(rb, 1<<3)

loop(i, 4)
	((aluop+i)<<12 | rd<<8 | ra<<4 | rb<<0) (rd)  #test add/sub/and/orr
end loop

	(ldrop    <<12 | rd<<8 | ra<<4 )        (rd)   #test ldr
	(strop    <<12 | rd<<8 | ra<<4 )        X     #test str
	
	let imm = random(256);
	(movlop   <<12 | rd<<8 | imm )          (rd)  #test movl

end loop
end loop
end loop
*/

/* Test case RS1:
	INST                                    RS1  

let aluop  = 0b1000;
let ldrop  = 0b0101;
let strop  = 0b0100;
let movlop = 0b0000;

loop(rd, 1<<3)
loop(ra, 1<<3)
loop(rb, 1<<3)

loop(i, 4)
	((aluop+i)<<12 | rd<<8 | ra<<4 | rb<<0) (ra)  #test add/sub/and/orr
end loop

	(ldrop    <<12 | rd<<8 | ra<<4 )        (ra)  #test ldr
	(strop    <<12 | rd<<8 | ra<<4 )        (ra)  #test str

end loop
end loop
end loop
*/

/* Test case RS2:
	INST                                    RS2  

let aluop  = 0b1000;
let ldrop  = 0b0101;
let strop  = 0b0100;
let movlop = 0b0000;

loop(rd, 1<<3)
loop(ra, 1<<3)
loop(rb, 1<<3)

loop(i, 4)
	((aluop+i)<<12 | rd<<8 | ra<<4 | rb<<0) (rb) #test add/sub/and/orr
end loop
	(strop    <<12 | rd<<8 | ra<<4 )        (rd) #test str

end loop
end loop
end loop
*/

/* Test case STR:
	INST                                    STR 

let aluop  = 0b1000;
let ldrop  = 0b0101;
let strop  = 0b0100;
let movlop = 0b0000;

loop(rd, 1<<3)
loop(ra, 1<<3)
loop(rb, 1<<3)

loop(i, 4)
	((aluop+i)<<12 | rd<<8 | ra<<4 | rb<<0) 0  #test add/sub/and/orr
end loop

	(ldrop    <<12 | rd<<8 | ra<<4 )        0  #test ldr
	(strop    <<12 | rd<<8 | ra<<4 )        1  #test str
	
	let imm = random(256);
	(movlop   <<12 | rd<<8 | imm )          0  #test movl

end loop
end loop
end loop
*/

/* Test case WE:
	INST    EXEC	                        WE  
let aluop  = 0b1000;
let ldrop  = 0b0101;
let strop  = 0b0100;
let movlop = 0b0000;

loop(rd, 1<<3)
loop(ra, 1<<3)
loop(rb, 1<<3)

loop(i, 4)
	let inst = ((aluop+i)<<12 | rd<<8 | ra<<4 | rb<<0) << 4;
	let inst = inst >> 15;
	((aluop+i)<<12 | rd<<8 | ra<<4 | rb<<0) 0  ((1-inst) | 0)  #test add/sub/and/orr
end loop
	let inst = (ldrop    <<12 | rd<<8 | ra<<4 ) << 4;
	let inst = inst >> 15;
	(ldrop    <<12 | rd<<8 | ra<<4 )        0  ((1-inst) | 0)  #test ldr

	let inst = (strop    <<12 | rd<<8 | ra<<4 ) << 4;
	let inst = inst >> 15;
	(strop    <<12 | rd<<8 | ra<<4 )        0  0  #test str
	
	let imm = random(256);
	let inst = (movlop   <<12 | rd<<8 | imm ) << 4;
	let inst = inst >> 15;
	(movlop   <<12 | rd<<8 | imm )          0  ((1-inst) | 0)  #test movl

end loop
end loop
end loop


let aluop  = 0b1000;
let ldrop  = 0b0101;
let strop  = 0b0100;
let movlop = 0b0000;

loop(rd, 1<<3)
loop(ra, 1<<3)
loop(rb, 1<<3)

loop(i, 4)
	let inst = ((aluop+i)<<12 | rd<<8 | ra<<4 | rb<<0) << 4;
	let inst = inst >> 15;
	((aluop+i)<<12 | rd<<8 | ra<<4 | rb<<0) 1  ((1-inst) | 1)  #test add/sub/and/orr
end loop
	let inst = (ldrop    <<12 | rd<<8 | ra<<4 ) << 4;
	let inst = inst >> 15;
	(ldrop    <<12 | rd<<8 | ra<<4 )        1  ((1-inst) | 1)  #test ldr

	let inst = (strop    <<12 | rd<<8 | ra<<4 ) << 4;
	let inst = inst >> 15;
	(strop    <<12 | rd<<8 | ra<<4 )        1  0  #test str
	
	let imm = random(256);
	let inst = (movlop   <<12 | rd<<8 | imm ) << 4;
	let inst = inst >> 15;
	(movlop   <<12 | rd<<8 | imm )          1  ((1-inst) | 1)  #test movl

end loop
end loop
end loop
*/

/* Test case LDR:
	INST                                    LDR 

let aluop  = 0b1000;
let ldrop  = 0b0101;
let strop  = 0b0100;
let movlop = 0b0000;
let ildrop = 0b0011;

loop(rd, 1<<3)
loop(ra, 1<<3)
loop(rb, 1<<3)

loop(i, 4)
	((aluop+i)<<12 | rd<<8 | ra<<4 | rb<<0) X    #test add/sub/and/orr
end loop

	(ldrop    <<12 | rd<<8 | ra<<4 )        1    #test ldr
	(strop    <<12 | rd<<8 | ra<<4 )        X    #test str
	(ildrop   <<12 | rd<<8 | ra<<4 )	1
	let imm = random(256);
	(movlop   <<12 | rd<<8 | imm )          X    #test movl

end loop
end loop
end loop
*/

/* Test case DMUX:
	INST                                    DMUX

let aluop  = 0b1000;
let ldrop  = 0b0101;
let strop  = 0b0100;
let movlop = 0b0000;

loop(rd, 1<<3)
loop(ra, 1<<3)
loop(rb, 1<<3)

loop(i, 4)
	((aluop+i)<<12 | rd<<8 | ra<<4 | rb<<0) 0  #test add/sub/and/orr
end loop

	(ldrop    <<12 | rd<<8 | ra<<4 )        1  #test ldr
	
	let imm = random(256);
	(movlop   <<12 | rd<<8 | imm )          2  #test movl

end loop
end loop
end loop
*/

/* Test case ALUOP:
	INST                                    ALUOP 

let aluop  = 0b1000;
let ldrop  = 0b0101;
let strop  = 0b0100;
let movlop = 0b0000;

loop(rd, 1<<3)
loop(ra, 1<<3)
loop(rb, 1<<3)

loop(i, 7)
	((aluop+i)<<12 | rd<<8 | ra<<4 | rb<<0) (i)    	#test add/sub/and/orr/xor/lsft/rsft
end loop

(0b1111<<12 | rd<<8 | ra<<4 | 0b0000<<0)  (0b0111)
(0b1111<<12 | rd<<8 | ra<<4 | 0b0010<<0)  (0b1000)
(0b1111<<12 | rd<<8 | ra<<4 | 0b0011<<0)  (0b1001)

end loop
end loop
end loop
*/

/* Test case FLEN:
	INST                                    FLEN

let aluop  = 0b1000;
let ldrop  = 0b0101;
let strop  = 0b0100;
let movlop = 0b0000;

loop(rd, 1<<3)
loop(ra, 1<<3)
loop(rb, 1<<3)

loop(i, 6)
	((aluop+i)<<12 | rd<<8 | ra<<4 | rb<<0) (1)    #test add/sub/and/orr
end loop

end loop
end loop
end loop
*/

/* Test case SFT:
INST SFT SFTM

loop (rd, 1<<3)
loop (ra, 1<<3)
loop (imm, 8)

(0b1101<<12 | rd<<8 | ra<<4 | 0<<3 | imm<<0) (imm) (0)
(0b1101<<12 | rd<<8 | ra<<4 | 1<<3 | imm<<0) (imm) (1)
(0b1110<<12 | rd<<8 | ra<<4 | 0<<3 | imm<<0) (imm) (0)
(0b1110<<12 | rd<<8 | ra<<4 | 1<<3 | imm<<0) (imm) (1)

end loop
end loop
end loop
*/
