// Digital circuit cpu.dig as structural Verilog
module cpu (
  input  CLK
);

  wire and_1_out, and_2_out, and_3_out, and_4_out, and_5_out, control_unit_1_flen, control_unit_1_ldr,
       control_unit_1_ra_control, control_unit_1_rb_control, control_unit_1_sftm, control_unit_1_str,
       control_unit_1_we, or_1_out;
  wire [1:0] control_unit_1_dmux, FL_q;
  wire [2:0] control_unit_1_rs1, control_unit_1_rs2, control_unit_1_sft, control_unit_1_ws,
       multiplexer_1_out, multiplexer_2_out;
  wire [3:0] alu_1_flag, control_unit_1_aluop;
  wire [7:0] RAM_d2;
  wire [15:0] alu_1_result, control_unit_1_imm8, multiplexer_3_out, multiplexer_4_out, multiplexer_5_out,
       multiplexer_6_out, multiplexer_7_out, multiplexer_8_out, multiplexer_9_out, PC_q, plus_1_s, RAM_d1,
       reg_file_1_out1, reg_file_1_out2;
  wire [15:2] FL_q_2;
  wire [15:8] RAM_d2_2;

  control_unit control_unit_1 (
    .INST({RAM_d2_2, RAM_d2}), .EXEC(FL_q), .ALUOP(control_unit_1_aluop), .RS1(control_unit_1_rs1),
    .RS2(control_unit_1_rs2), .WS(control_unit_1_ws), .STR(control_unit_1_str), .WE(control_unit_1_we),
    .DMUX(control_unit_1_dmux), .LDR(control_unit_1_ldr), .FLEN(control_unit_1_flen),
    .Ra_control(control_unit_1_ra_control), .Rb_control(control_unit_1_rb_control),
    .IMM8(control_unit_1_imm8), .SFT(control_unit_1_sft), .SFTM(control_unit_1_sftm));
  and and_1 (and_1_out, control_unit_1_ws[0], control_unit_1_ws[1], control_unit_1_ws[2]);
  and and_2 (and_2_out, RAM_d2_2[12], ~RAM_d2_2[13], ~RAM_d2_2[14], ~RAM_d2_2[15]);  // And
  and and_3 (and_3_out, ~RAM_d2_2[14], ~RAM_d2_2[15], RAM_d2_2[13], RAM_d2_2[12]);  // And
  Multiplexer #(.Bits(3)) multiplexer_1 (
    .sel(and_2_out), .in_0(control_unit_1_ws), .in_1(RAM_d2_2[10:8]), .out(multiplexer_1_out));
  or or_1 (or_1_out, control_unit_1_we, and_2_out);
  Multiplexer #(.Bits(3)) multiplexer_2 (
    .sel(and_2_out), .in_0(control_unit_1_rs1), .in_1(RAM_d2_2[10:8]), .out(multiplexer_2_out));
  Multiplexer #(.Bits(16)) multiplexer_3 (
    .sel(and_2_out), .in_0(multiplexer_9_out), .in_1({RAM_d2, reg_file_1_out1[7:0]}), .out(multiplexer_3_out));
  Multiplexer #(.Bits(16)) multiplexer_4 (
    .sel(and_1_out), .in_0(plus_1_s), .in_1(multiplexer_9_out), .out(multiplexer_4_out));
  and and_4 (and_4_out, or_1_out, control_unit_1_flen);
  reg_file reg_file_1 (
    .RS1(multiplexer_2_out), .RS2(control_unit_1_rs2), .WS(multiplexer_1_out), .WE(or_1_out),
    .IN(multiplexer_3_out), .clk(CLK), .OUT1(reg_file_1_out1), .OUT2(reg_file_1_out2));
  Register #(.Bits(16), .isProgramCounter("true")) PC (.D(multiplexer_4_out), .C(CLK), .en(1'b1), .Q(PC_q));
  Register #(.Bits(16)) FL (.D({{12{1'b0}}, alu_1_flag}), .C(CLK), .en(and_4_out), .Q({FL_q_2, FL_q}));
  Add #(.Bits(16)) plus_1 (.a(16'h1), .b(PC_q), .c_i(1'b0), .s(plus_1_s));  // open: c_o
  and and_5 (and_5_out, RAM_d2_2[12], RAM_d2_2[13], RAM_d2_2[14], RAM_d2_2[15]);
  Multiplexer #(.Selector_Bits(3), .Bits(16)) multiplexer_5 (
    .sel(control_unit_1_rs1), .in_0(reg_file_1_out1), .in_1(reg_file_1_out1), .in_2(reg_file_1_out1),
    .in_3(reg_file_1_out1), .in_4(reg_file_1_out1), .in_5({FL_q_2, FL_q}), .in_6({16{1'b0}}), .in_7(PC_q),
    .out(multiplexer_5_out));
  Multiplexer #(.Selector_Bits(3), .Bits(16)) multiplexer_6 (
    .sel(control_unit_1_rs2), .in_0(reg_file_1_out2), .in_1(reg_file_1_out2), .in_2(reg_file_1_out2),
    .in_3(reg_file_1_out2), .in_4(reg_file_1_out2), .in_5({FL_q_2, FL_q}), .in_6({16{1'b0}}), .in_7(PC_q),
    .out(multiplexer_6_out));
  Multiplexer #(.Bits(16)) multiplexer_7 (
    .sel(and_3_out), .in_0(reg_file_1_out1), .in_1(control_unit_1_imm8), .out(multiplexer_7_out));
  Multiplexer #(.Bits(16)) multiplexer_8 (
    .sel(and_5_out), .in_0({{8{1'b0}}, RAM_d2}), .in_1({RAM_d2_2, RAM_d2}), .out(multiplexer_8_out));
  Multiplexer #(.Selector_Bits(2), .Bits(16)) multiplexer_9 (
    .sel(control_unit_1_dmux), .in_0(alu_1_result), .in_1(RAM_d1), .in_2(multiplexer_8_out), .in_3(16'h1),
    .out(multiplexer_9_out));
  alu alu_1 (
    .A(multiplexer_5_out), .B(multiplexer_6_out), .ALUOP(control_unit_1_aluop),
    .Ra_controlIn(control_unit_1_ra_control), .Rb_controlO(control_unit_1_rb_control),
    .SFT(control_unit_1_sft), .SFTM(control_unit_1_sftm), .RESULT(alu_1_result), .FLAG(alu_1_flag));
  RAMDualAccess #(.AddrBits(16), .isProgramMemory("true"), .Bits(16)) RAM (
    .str(control_unit_1_str), .C(CLK), .ld(control_unit_1_ldr), .A1(multiplexer_7_out),
    .Din1(reg_file_1_out2), .A2(PC_q), .D1(RAM_d1), .D2({RAM_d2_2, RAM_d2}));
endmodule
