// Digital circuit alu.dig as structural Verilog
module alu (
  input  [15:0] A,
  input  [15:0] B,
  input  [3:0] ALUOP,
  input  Ra_controlIn,
  input  Rb_controlO,
  input  [2:0] SFT,
  input  SFTM,
  output [15:0] RESULT,
  output [3:0] FLAG
);

  wire add_1_c_o, and_1_out, or_2_out, xor_3_out, xor_4_out;
  wire [14:0] multiplexer_2_out;
  wire [15:0] add_1_s, and_2_out, bit_shifter_1_out, multiplexer_1_out, multiplexer_3_out, multiplexer_4_out,
       not_1_out, OP_0_out, or_1_out, xor_1_out, xor_2_out;

  bit_shifter bit_shifter_1 (.SFT(SFT), .M(SFTM), .IN(A), .DIR(ALUOP[0]), .OUT(bit_shifter_1_out));
  merger_16to1 OP_0 (.IN(ALUOP[0]), .OUT(OP_0_out));
  Multiplexer #(.Bits(16)) multiplexer_1 (.sel(ALUOP[3]), .in_0(B), .in_1(16'h1), .out(multiplexer_1_out));
  assign xor_1_out = multiplexer_1_out ^ OP_0_out;  // XOr xor_1, 16 bits wide
  and and_1 (and_1_out, ~ALUOP[1], ~ALUOP[2]);  // And
  assign and_2_out = B & A;  // And and_2, 16 bits wide
  assign or_1_out = B | A;  // Or or_1, 16 bits wide
  Add #(.Bits(16)) add_1 (.a(A), .b(xor_1_out), .c_i(ALUOP[0]), .s(add_1_s), .c_o(add_1_c_o));
  assign xor_2_out = B ^ A;  // XOr xor_2, 16 bits wide
  assign not_1_out = ~A;  // Not not_1, 16 bits wide
  and and_3 (FLAG[2], add_1_c_o, and_1_out);
  Multiplexer #(.Selector_Bits(3), .Bits(16)) multiplexer_2 (
    .sel(ALUOP[2:0]), .in_0(add_1_s), .in_1(add_1_s), .in_2(and_2_out), .in_3(or_1_out), .in_4(xor_2_out),
    .in_5(bit_shifter_1_out), .in_6(bit_shifter_1_out), .in_7(not_1_out), .out({FLAG[1], multiplexer_2_out}));
  Multiplexer #(.Bits(16)) multiplexer_3 (
    .sel(ALUOP[3]), .in_0({FLAG[1], multiplexer_2_out}), .in_1(add_1_s), .out(multiplexer_3_out));
  Multiplexer #(.Bits(16)) multiplexer_4 (
    .sel(Ra_controlIn), .in_0(multiplexer_3_out), .in_1(A), .out(multiplexer_4_out));
  xor xor_3 (xor_3_out, FLAG[1], xor_1_out[15]);
  xor xor_4 (xor_4_out, FLAG[1], A[15]);
  or or_2 (or_2_out, multiplexer_3_out[0], multiplexer_3_out[1], multiplexer_3_out[2], multiplexer_3_out[3], multiplexer_3_out[4], multiplexer_3_out[5], multiplexer_3_out[6], multiplexer_3_out[7], multiplexer_3_out[9], multiplexer_3_out[10], multiplexer_3_out[11], multiplexer_3_out[12], multiplexer_3_out[13], multiplexer_3_out[14], multiplexer_3_out[15], multiplexer_3_out[8]);
  Multiplexer #(.Bits(16)) multiplexer_5 (.sel(Rb_controlO), .in_0(multiplexer_4_out), .in_1(B), .out(RESULT));
  not not_2 (FLAG[0], or_2_out);
  and and_4 (FLAG[3], xor_3_out, xor_4_out, and_1_out);
  // NotConnected on nothing
  // NotConnected on nothing

  // Notes on the sheet:
  //   A: First input to ALU
  //   B: Second input to ALU
  //   ALUOP: Operation selection input
  //   RESULT: The result of this ALU operation
  //   FLAG: The flags associated with the result of this ALU operation
  //   0. Z (zero)
  //   1. N (negative)
  //   2. C (carry)
  //   3. V (overflow)
  //   Ra_controlIn: The control signal that require alu to out put ra
  //   Rb_controlO: The control signal that require alu to output rb
endmodule

/* Test case RESULT:
ALUOP A B SFT SFTM RESULT

# Test small results
loop(a, 1 << 4)
loop(b, 1 << 4)

    (0b0000) (a) (b) x x ((a + b) & 0xFFFF)
    (0b0001) (a) (b) x x ((a - b) & 0xFFFF)
    (0b0010) (a) (b) x x (a & b)
    (0b0011) (a) (b) x x (a | b)
    (0b0100) (a) (b) x x (a ^ b)
    (0b0111) (a) (b) x x (a ^ 0xFFFF)
    (0b1000) (a) (b) x x ((a + 1) & 0xFFFF)
    (0b1001) (a) (b) x x ((a - 1) & 0xFFFF)
loop(s, 8)
    (0b0101) (a) (b) (s) (0) (a<<s)  # left shift
    (0b0110) (a) (b) (s) (0) (a>>s) # rsft
end loop
end loop
end loop


# Test large results
loop(i, 1000)
    let a = random(1 << 16);
    let b = random(1 << 16);

    (0b0000) (a) (b) x x ((a + b) & 0xFFFF)
    (0b0001) (a) (b) x x ((a - b) & 0xFFFF)
    (0b0010) (a) (b) x x (a & b)
    (0b0011) (a) (b) x x (a | b)
    (0b0100) (a) (b) x x (a ^ b)
    (0b0111) (a) (b) x x (a ^ 0xFFFF)
    (0b1000) (a) (b) x x ((a + 1) & 0xFFFF)
    (0b1001) (a) (b) x x ((a - 1) & 0xFFFF)
loop(s, 8)
    (0b0101) (a) (b) (s) (0) (a<<s)  # left shift
    (0b0110) (a) (b) (s) (0) (a>>s) # rsft
end loop
end loop
*/

/* Test case Z:
ALUOP A B Z

declare Z = FLAG & 0b1;

# Test all zero cases
0b0000 0 0 1
0b0001 0 0 1
0b0010 0 0 1
0b0011 0 0 1

# Test 1 + (-1) = 0
00 1 0xFFFF 1

# Test with a single bit set in A
loop(s, 16)
    let a = 1 << s;

    0b0000 (a) 0 (a = 0)
    0b0001 (a) 0 (a = 0)
    0b0010 (a) 0 1
    0b0011 (a) 0 (a = 0)
end loop

# Test random inputs
loop(i, 200)
    let a = random(1 << 16);
    let b = random(1 << 16);

    0b0000 (a) (b) (((a + b) & 0xFFFF) = 0)
    0b0001 (a) (b) (((a - b) & 0xFFFF) = 0)
    0b0010 (a) (b) ((a & b) = 0)
    0b0011 (a) (b) ((a | b) = 0)
end loop
*/

/* Test case N:
ALUOP A B SFT SFTM N

declare N = (FLAG >> 1) & 0b1;

# Test all zero cases
0b0000 0 0 x x 0
0b0001 0 0 x x 0
0b0010 0 0 x x 0
0b0011 0 0 x x 0
0b0100 0 0 x x 0
0b0101 0 0 x x 0
0b0110 0 0 x x 0
0b0111 0 0 x x 1
0b1000 0 0 x x 0
0b1001 0 0 x x 1

0b0000 1 0xFFFF x x 0

# Test with a single bit set in A
loop(s, 16)
    let a = 1 << s;

    0b0000 (a) 0 x x ((a >> 15) & 0b1)
    0b1001 (a) 0 x x (((a-1)>> 15) & 0b1)
end loop

# Test random inputs
loop(i, 200)
    let a = random(1 << 16);
    let b = random(1 << 16);

    
    0b0000 (a) (b) x x (((a + b) >> 15) & 0b1)
    0b0001 (a) (b) x x (((a - b) >> 15) & 0b1)
    0b0010 (a) (b) x x (((a & b) >> 15) & 0b1)
    0b0011 (a) (b) x x (((a | b) >> 15) & 0b1)
    0b0100 (a) (b) x x (((a ^ b) >> 15) & 0b1)
    0b0111 (a) (b) x x (((0xFFFF - a) >> 15) & 0b1)
    0b1000 (a) (b) x x (((a + 1) >> 15) & 0b1)
    0b1001 (a) (b) x x (((a - 1) >> 15) & 0b1)
loop(s, 8)
    0b0101 (a) (b) (s) 0 ((((a<<s)) >> 15) & 0b1)   
 #   0b0101 (a) (b) (s) 1 (((((i<<s)|(i>>(16-s)))) >> 15) & 0b1)
    0b0110 (a) (b) (s) 0 ((((a>>s)) >> 15) & 0b1) 
 #   0b0110 (a) (b) (s) 1 (((((i<<(16-s))|(i>>s))) >> 15) & 0b1) 
end loop

end loop
*/

/* Test case C:
ALUOP A B C

declare C = (FLAG >> 2) & 0b1;

0b0000 0 0 0

# (0 - 0) is implemented as 0 + (0xFFFF + 1), so a carry is expected
0b0001 0 0 1

# Carry should propagate all the way from the first bit if necessary
0b0000 1 0xFFFF 1

# Test with a single bit set in A
loop(s, 16)
    let a = 1 << s;

    0b0000 (a) 0 0
    0b0001 (a) 0 1  # (a - 0) is implemented as (a + 0xFFFF + 1) in the adder, so a carry is always expected
    0b0010 (a) 0 0  # carry is defined as 0 for AND
    0b0011 (a) 0 0  # carry is defined as 0 for OR
    0b0100 (a) 0 0  # xor
    0b0101 (a) 0 0  # left shift 
    0b0110 (a) 0 0  # right shift
    0b0111 (a) 0 0  # not
    0b1000 (a) 0 (((a+1)>>16) & 1)
    0b1001 (a) 0 1  # (((a-1)>>16) & 1)
end loop

# Adding 15 bit values should never carry
loop(i, 100)
    0b0000 (random(1 << 15)) (random(1 << 15)) 0
end loop

# Test random inputs
loop(i, 200)
    let a = random(1 << 16);
    let b = random(1 << 16);

    0b0000 (a) (b) (((a + b) >> 16) & 0b1)
    0b0001 (a) (b) (~((a - b) >> 16) & 0b1)
    
end loop

# AND, OR, XOR, NOT, left shift, right shift never set carry
loop(i, 100)
    let a = random(1 << 16);
    let b = random(1 << 16);
    0b0010 (a) (b) 0
    0b0011 (a) (b) 0
    0b0111 (a) (b) 0
    0b0100 (a) (b) 0
end loop
*/

/* Test case V:
ALUOP A B V

declare V = (FLAG >> 3) & 0b1;

0b0000 0 0 0
0b0001 0 0 0

# 1 + (-1) = 0  ; different input signs = no overflow here!
0b0000 1 0xFFFF 0

# 3 - 5 = 3 + (-5) = -2  ; subtraction inverts the second operand sign
0b0001 3 5 0

# Some edge cases when subtracting 0x8000
0b0001 0x8000 0x8000 0
0b0001 0xFFFF 0x8000 0
0b0001 0x7FFF 0x8000 1

# Test with a single bit set in A
loop(s, 16)
    let a = 1 << s;

    0b0000 (a) 0 0
    0b0001 (a) 0 0
    0b0010 (a) 0 0  # overflow is defined as 0 for AND
    0b0011 (a) 0 0  # overflow is defined as 0 for OR
    0b0100 (a) 0 0  # XOR
    0b0101 (a) 0 0  # lsft
    0b0110 (a) 0 0  # rsft
    0b0111 (a) 0 0  # not
    0b1000 (a) 0 0
#    0b1001 (a) 0 x
end loop

# Test random inputs
loop(i, 200)
    let a = random(1 << 16);
    let b = random(1 << 16);

    0b0000 (a) (b) (((~(a ^ b) & (a ^ (a + b))) >> 15) & 0b1)
    0b0001 (a) (b) (((~(a ^ -b) & (a ^ (a - b))) >> 15) & 0b1)
    0b1000 (a) (b) (((~(a ^ 1) & (a ^ (a + 1))) >> 15) & 0b1)
    0b1001 (a) (b) (((~(a ^ -1) & (a ^ (a - 1))) >> 15) & 0b1)
end loop

# AND and OR never set overflow
loop(i, 100)
    let a = random(1 << 16);
    let b = random(1 << 16);
    0b0010 (a) 0 0  # overflow is defined as 0 for AND
    0b0011 (a) 0 0  # overflow is defined as 0 for OR
    0b0100 (a) 0 0  # xor
    0b0111 (a) 0 0  # not
    0b0101 (a) 0 0  # lsft
    0b0110 (a) 0 0  # rsft
end loop
*/
